# Fritzing sketch RFClicker2 (saved by Fritzing 0.9.4)
circuit board: 8.46667cm x 5.64444cm
stripboards: 2

parts:
  RIGHT = Momentary Switch [package=ksa_sealed_tac_switch]
  LEFT = Momentary Switch [package=ksa_sealed_tac_switch]
  UP = Momentary Switch [package=ksa_sealed_tac_switch]
  DOWN = Momentary Switch [package=ksa_sealed_tac_switch]
  IC1 = 24LC256 [package=THT]
  Part1 = Arduino Nano 33 IOT
  BTMENU = 3 Legged Button [package=ksa_sealed_tac_switch]
  POWER = 3 Legged Button (South) [package=ksa_sealed_tac_switch]
  MENULEFT = 3 Legged Button [package=ksa_sealed_tac_switch]
  Part2 = OLED 0.96" 128x64 I2C SSD1306
  MENULEFT_2 = 3 Legged Button (South) [package=ksa_sealed_tac_switch]
  U2 = LIPO-1000mAh [package=lipo-1000]
  Part3 = IP5306 Boost

nets:
  N1: RIGHT.2, Part1.D5~
  N2: RIGHT.3, UP.1, UP.2
  N3: RIGHT.4, LEFT.1, MENULEFT.3, Part2.GND
  GND: LEFT.2, DOWN.3, DOWN.4, IC1.A0, IC1.A1, IC1.A2, IC1.0V, IC1.WP_-_Write_Protect, Part1.GND, Part1.D13~, Part3.GND
  N4: LEFT.4, Part1.D7
  3V3: UP.3, UP.4, IC1.+V, Part1.D9~, Part1.3V3, Part2.VCC
  N5: DOWN.1, DOWN.2, Part1.D6~
  N6: IC1.SDA_-_I2C_Data, Part1.A4, Part2.SCA
  N7: IC1.SCL_-_I2C_Clock, Part1.A5, Part2.SCL
  N8: Part1.RESET, Part1.A7
  N9: Part1.D2, BTMENU.2
  N10: Part1.D3~, POWER.1, Part3.RESET
  N11: Part1.D4, MENULEFT.2
  N12: Part1.D8, MENULEFT_2.3
  +5V: Part1.D11/MOSI, Part1.+5V, Part3.VIN
  N13: Part1.VIN, Part3.OUT_5V
  N14: BTMENU.3, POWER.3, MENULEFT.1
  N15: POWER.2, MENULEFT_2.1
  N16: U2.+, Part3.BAT+
  N17: U2.-, Part3.BAT-

custom parts:
  Arduino Nano 33 IOT: The Arduino Nano 33 IoT is the easiest and cheapest point of entry to enhance existing devices (and creating new ones) to be part of the IoT and designing pico-network applications. Whether you are looking at building a sensor network connected to your office or home router, or if you want to create a BLE device sending data to a cellphone, the Nano 33 IoT is your one-stop-solution for many of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
  IP5306 Boost: IP5306 Charge/Discharge/Boost Module
